# Fritzing sketch GPS tracking with nodemcu (saved by Fritzing 0.9.3b)

parts:
  GY-NEO6MV2 = SUP500F [package=sup500f]
  U3 = ESP8266 NodeMCU LoLin module

nets:
  N1: GY-NEO6MV2.RX-I, U3.GND
  N2: GY-NEO6MV2.TX-O, U3.SK
  N3: GY-NEO6MV2.GND, U3.D1
  N4: GY-NEO6MV2.VCC, U3.D2

notes:
  GND: Black
  VCC: Red
  RX: Yellow
  TX: Green

custom parts:
  ESP8266 NodeMCU LoLin module: ESP8266 based NodeMCU
