# Fritzing sketch rfid (saved by Fritzing 0.9.3b)

parts:
  Part2 = RFID-RC522-v2
  U3 = ESP8266 NodeMCU LoLin module
  J1 = Piezo Speaker

nets:
  N1: Part2.SDA, U3.D4
  N2: Part2.SCK, U3.D5
  N3: Part2.MOSI, U3.D7
  N4: Part2.MISO, U3.D6
  GND: Part2.GND, U3.GND
  N5: Part2.RST, U3.D3
  3.3V: Part2.3.3V, U3.3V3
  N6: U3.D2, J1.pin2

custom parts:
  RFID-RC522-v2: A simple China made RFID-RC522 Reader; do check the pin labels, as this is a MFRC522 based clone.
  ESP8266 NodeMCU LoLin module: ESP8266 based NodeMCU
